// Logisim project 10 bit mips.circ as structural Verilog: 5 circuits, main circuit 10 bit MIPS
module _10_bit_MIPS (
  input  in_1,
  input  in_2,
  input  clear,
  output out_4
);

  wire and_1_out, clock_out, control_unit_1_alusrc, control_unit_1_branch, control_unit_1_memread,
       control_unit_1_memtoreg, control_unit_1_memwrite, control_unit_1_regdst, control_unit_1_regwrite,
       n10_bit_alu_1_flag;
  wire [1:0] control_unit_1_aluop, multiplexer_1_out;
  wire [3:0] adder_1_out, adder_2_out, multiplexer_3_out, register_1_q, rom_1_data;
  wire [5:0] rom_1_data_2;
  wire [9:0] bit_extender_1_out, multiplexer_2_out, multiplexer_4_out, n10_bit_alu_1_aluout, ram_1_data,
       register_2_read_data_1, register_2_read_data_2;

  Register_part #(.width(4)) register_1 (
    .D(multiplexer_3_out), .Q(register_1_q), .clk(clock_out), .clr(clear));  // open: en
  Adder #(.width(4)) adder_1 (.a(register_1_q), .b(4'b0001), .out(adder_1_out));  // open: cin, cout
  Clock clock (.out(clock_out));
  ROM #(.addrWidth(4), .dataWidth(10)) rom_1 (.addr(register_1_q), .data({rom_1_data, rom_1_data_2}));  // open: sel
  Control_unit control_unit_1 (
    .Opcode(rom_1_data), .RegDst(control_unit_1_regdst), .ALUSrc(control_unit_1_alusrc),
    .MemToReg(control_unit_1_memtoreg), .RegWrite(control_unit_1_regwrite), .MemRead(control_unit_1_memread),
    .MemWrite(control_unit_1_memwrite), .ALUOp(control_unit_1_aluop), .Branch(control_unit_1_branch));
  Multiplexer #(.width(2), .enable("false")) multiplexer_1 (
    .in0(rom_1_data_2[3:2]), .in1(rom_1_data_2[1:0]), .out(multiplexer_1_out), .sel(control_unit_1_regdst));
  assign bit_extender_1_out = {{8{1'b0}}, rom_1_data_2[1:0]};  // Bit_Extender bit_extender_1
  Register register_2 (
    .regWrite(control_unit_1_regwrite), .write_data(multiplexer_4_out), .clock(clock_out),
    .rd(multiplexer_1_out), .rs(rom_1_data_2[5:4]), .rt(rom_1_data_2[3:2]),
    .Read_Data_1(register_2_read_data_1), .Read_Data_2(register_2_read_data_2));  // open: clear
  Adder #(.width(4)) adder_2 (
    .a(adder_1_out), .b({rom_1_data[3:2], rom_1_data_2[1:0]}), .out(adder_2_out));  // open: cin, cout
  Multiplexer #(.width(10), .enable("false")) multiplexer_2 (
    .in0(register_2_read_data_2), .in1(bit_extender_1_out), .out(multiplexer_2_out),
    .sel(control_unit_1_alusrc));
  Multiplexer #(.width(4), .enable("false")) multiplexer_3 (
    .in0(adder_1_out), .in1(adder_2_out), .out(multiplexer_3_out), .sel(and_1_out));
  and and_1 (and_1_out, control_unit_1_branch, n10_bit_alu_1_flag);
  _10_bit_ALU u_10_bit_alu_1 (
    .A(register_2_read_data_1), .B(multiplexer_2_out), .ALUop(control_unit_1_aluop), .Cin(in_2),
    .ALUout(n10_bit_alu_1_aluout), .cout(out_4), .flag(n10_bit_alu_1_flag), .Bin(in_1));
  RAM #(.addrWidth(10), .dataWidth(10), .bus("separate")) ram_1 (
    .addr(n10_bit_alu_1_aluout), .din(register_2_read_data_2), .data(ram_1_data),
    .str(control_unit_1_memwrite), .clk(clock_out), .ld(control_unit_1_memread));  // open: sel, clr
  Multiplexer #(.width(10), .enable("false")) multiplexer_4 (
    .in0(ram_1_data), .in1(n10_bit_alu_1_aluout), .out(multiplexer_4_out), .sel(control_unit_1_memtoreg));

  // Notes on the sheet:
  //   contents of rom_1 (hex, n*v repeats v):
  //   84 2 3 124 3b 3b 69 203 cd
  //   OP:9-6, RS:5-4, RT:3-2, RD:1-0
  //   RegDst
  //   MemToReg
endmodule

module Register (
  input  regWrite,
  input  [9:0] write_data,
  input  clock,
  input  [1:0] rd,
  input  clear,
  input  [1:0] rs,
  input  [1:0] rt,
  output [9:0] Read_Data_1,
  output [9:0] Read_Data_2
);

  wire and_1_out, and_2_out, and_3_out, and_4_out, decoder_1_out0, decoder_1_out1, decoder_1_out2,
       decoder_1_out3;
  wire [9:0] register_1_q, register_2_q, register_3_q, register_4_q;

  Decoder #(.select(2), .enable("false")) decoder_1 (
    .out0(decoder_1_out0), .out1(decoder_1_out1), .out2(decoder_1_out2), .out3(decoder_1_out3), .sel(rd));
  and and_1 (and_1_out, decoder_1_out0, regWrite);
  and and_2 (and_2_out, decoder_1_out1, regWrite);
  and and_3 (and_3_out, decoder_1_out2, regWrite);
  and and_4 (and_4_out, decoder_1_out3, regWrite);
  Register_part #(.width(10)) register_1 (.D({10{1'b0}}), .en(and_1_out), .Q(register_1_q), .clk(clock), .clr(clear));
  Register_part #(.width(10)) register_2 (.D(write_data), .en(and_2_out), .Q(register_2_q), .clk(clock), .clr(clear));
  Register_part #(.width(10)) register_3 (.D(write_data), .en(and_3_out), .Q(register_3_q), .clk(clock), .clr(clear));
  Register_part #(.width(10)) register_4 (.D(write_data), .en(and_4_out), .Q(register_4_q), .clk(clock), .clr(clear));
  Multiplexer #(.select(2), .width(10), .enable("false")) multiplexer_1 (
    .in0(register_1_q), .in1(register_2_q), .in2(register_3_q), .in3(register_4_q), .out(Read_Data_1),
    .sel(rs));
  Multiplexer #(.select(2), .width(10), .enable("false")) multiplexer_2 (
    .in0(register_1_q), .in1(register_2_q), .in2(register_3_q), .in3(register_4_q), .out(Read_Data_2),
    .sel(rt));

  // Notes on the sheet:
  //   Zero
  //   x
  //   to
  //   i
  //   t1
  //   sum
  //   t2
endmodule

module Control_unit (
  input  [3:0] Opcode,
  output RegDst,
  output ALUSrc,
  output MemToReg,
  output RegWrite,
  output Branch,
  output MemRead,
  output MemWrite,
  output [1:0] ALUOp
);

  wire addi_out, BEQ_4_out, BEQ_11_out;

  and R_type (RegDst, ~Opcode[3], ~Opcode[2], ~Opcode[1], ~Opcode[0]);  // AND_Gate
  and addi (addi_out, ~Opcode[3], ~Opcode[2], ~Opcode[1], Opcode[0]);  // AND_Gate
  and lw (MemRead, ~Opcode[3], ~Opcode[2], Opcode[1], ~Opcode[0]);  // AND_Gate
  and sw (MemWrite, ~Opcode[3], ~Opcode[2], Opcode[1], Opcode[0]);  // AND_Gate
  and BEQ_4 (BEQ_4_out, ~Opcode[3], Opcode[2], ~Opcode[1], ~Opcode[0]);  // AND_Gate
  or or_1 (ALUOp[1], MemWrite, addi_out, 1'b1, RegDst, MemRead);
  and BEQ_11 (BEQ_11_out, Opcode[3], ~Opcode[2], ~Opcode[1], ~Opcode[0]);  // AND_Gate
  or or_2 (MemToReg, RegDst, addi_out);
  or or_3 (ALUOp[0], BEQ_11_out, BEQ_4_out);
  or or_4 (ALUSrc, MemWrite, addi_out, MemRead);
  or or_5 (RegWrite, RegDst, addi_out, MemRead);
  or or_6 (Branch, BEQ_4_out, BEQ_11_out);
endmodule

module _1bit_ALU (
  input  Carry_in___Borrow_in,
  input  A,
  input  B,
  input  [1:0] select,
  input  Bin,
  output RESULT,
  output Carryout____Borrow_out
);

  wire adder_1_out, and_1_out, multiplexer_1_out, not_1_out, or_1_out;

  not not_1 (not_1_out, B);
  Multiplexer #(.enable("false")) multiplexer_1 (.in0(B), .in1(not_1_out), .out(multiplexer_1_out), .sel(Bin));
  and and_1 (and_1_out, A, B);
  or or_1 (or_1_out, A, B);
  Adder #(.width(1)) adder_1 (
    .a(A), .b(multiplexer_1_out), .out(adder_1_out), .cin(Carry_in___Borrow_in), .cout(Carryout____Borrow_out));
  Multiplexer #(.select(2), .enable("false")) multiplexer_2 (
    .in0(and_1_out), .in1(or_1_out), .in2(adder_1_out), .out(RESULT), .sel(select));  // open: in3
endmodule

module _10_bit_ALU (
  input  Bin,
  input  Cin,
  input  [9:0] A,
  input  [9:0] B,
  input  [1:0] ALUop,
  output [9:0] ALUout,
  output cout,
  output flag
);

  wire n1bit_alu_1_carryout____borrow_out, n1bit_alu_2_carryout____borrow_out,
       n1bit_alu_3_carryout____borrow_out, n1bit_alu_4_carryout____borrow_out,
       n1bit_alu_5_carryout____borrow_out, n1bit_alu_6_carryout____borrow_out,
       n1bit_alu_7_carryout____borrow_out, n1bit_alu_8_carryout____borrow_out,
       n1bit_alu_9_carryout____borrow_out;

  _1bit_ALU u_1bit_alu_1 (
    .A(A[0]), .B(B[0]), .RESULT(ALUout[0]), .Carryout____Borrow_out(n1bit_alu_1_carryout____borrow_out),
    .Carry_in___Borrow_in(Cin), .select(ALUop), .Bin(Bin));
  _1bit_ALU u_1bit_alu_2 (
    .A(A[1]), .B(B[1]), .RESULT(ALUout[1]), .Carryout____Borrow_out(n1bit_alu_2_carryout____borrow_out),
    .Carry_in___Borrow_in(n1bit_alu_1_carryout____borrow_out), .select(ALUop), .Bin(Bin));
  _1bit_ALU u_1bit_alu_3 (
    .A(A[2]), .B(B[2]), .RESULT(ALUout[2]), .Carryout____Borrow_out(n1bit_alu_3_carryout____borrow_out),
    .Carry_in___Borrow_in(n1bit_alu_2_carryout____borrow_out), .select(ALUop), .Bin(Bin));
  _1bit_ALU u_1bit_alu_4 (
    .A(A[3]), .B(B[3]), .RESULT(ALUout[3]), .Carryout____Borrow_out(n1bit_alu_4_carryout____borrow_out),
    .Carry_in___Borrow_in(n1bit_alu_3_carryout____borrow_out), .select(ALUop), .Bin(Bin));
  _1bit_ALU u_1bit_alu_5 (
    .A(A[4]), .B(B[4]), .RESULT(ALUout[4]), .Carryout____Borrow_out(n1bit_alu_5_carryout____borrow_out),
    .Carry_in___Borrow_in(n1bit_alu_4_carryout____borrow_out), .select(ALUop), .Bin(Bin));
  _1bit_ALU u_1bit_alu_6 (
    .A(A[5]), .B(B[5]), .RESULT(ALUout[5]), .Carryout____Borrow_out(n1bit_alu_6_carryout____borrow_out),
    .Carry_in___Borrow_in(n1bit_alu_5_carryout____borrow_out), .select(ALUop), .Bin(Bin));
  _1bit_ALU u_1bit_alu_7 (
    .A(A[6]), .B(B[6]), .RESULT(ALUout[6]), .Carryout____Borrow_out(n1bit_alu_7_carryout____borrow_out),
    .Carry_in___Borrow_in(n1bit_alu_6_carryout____borrow_out), .select(ALUop), .Bin(Bin));
  _1bit_ALU u_1bit_alu_8 (
    .A(A[7]), .B(B[7]), .RESULT(ALUout[7]), .Carryout____Borrow_out(n1bit_alu_8_carryout____borrow_out),
    .Carry_in___Borrow_in(n1bit_alu_7_carryout____borrow_out), .select(ALUop), .Bin(Bin));
  _1bit_ALU u_1bit_alu_9 (
    .A(A[8]), .B(B[8]), .RESULT(ALUout[8]), .Carryout____Borrow_out(n1bit_alu_9_carryout____borrow_out),
    .Carry_in___Borrow_in(n1bit_alu_8_carryout____borrow_out), .select(ALUop), .Bin(Bin));
  _1bit_ALU u_1bit_alu_10 (
    .A(A[9]), .B(B[9]), .RESULT(ALUout[9]), .Carryout____Borrow_out(cout),
    .Carry_in___Borrow_in(n1bit_alu_9_carryout____borrow_out), .select(ALUop), .Bin(Bin));
  Comparator #(.width(10)) comparator_1 (.a(A), .b(B), .eq(flag));  // open: gt, lt
endmodule
